# Fritzing sketch Alarm (saved by Fritzing 0.9.3b)
breadboards: 1

parts:
  Part1 = Arduino Uno (Rev3)
  LED1 = RGB LED (com. cathode, rgb) [package="5 mm [THT]"]
  hc-sr1 = hc-sr04
  Q1 = Basic FET N-Channel [package="D2Pak [SMD]"]
  Q2 = Basic FET N-Channel [package="D2Pak [SMD]"]
  Q3 = Basic FET N-Channel [package="D2Pak [SMD]"]
  J1 = Piezo Speaker
  S1 = Momentary Switch [package=ksa_sealed_tac_switch]
  S2 = Momentary Switch [package=ksa_sealed_tac_switch]
  R1 = Resistor [tolerance=±5% resistance=220 package="2512 [SMD]"]
  R2 = Resistor [tolerance=±5% resistance=220 package="2512 [SMD]"]

nets:
  N1: Part1.D9_PWM, Q3.Gate
  N2: Part1.D10_PWM/SS, Q2.Gate
  N3: Part1.D11_PWM/MOSI, Q1.Gate
  N4: Part1.D12/MISO, S2.2
  N5: Part1.D13/SCK, S1.2
  N6: Part1.D3_PWM, J1.pin1
  N7: Part1.D6_PWM, hc-sr1.Trig
  N8: Part1.D7, hc-sr1.Echo
  5V: Part1.5V, LED1.red_anode, hc-sr1.VCC
  GND: Part1.GND, hc-sr1.GND, Q1.source, Q2.source, Q3.source, J1.pin2, S1.4, S2.4
  N9: LED1.common_cathode, Q1.drain
  N10: LED1.green_anode, Q2.drain
  N11: LED1.blue_anode, Q3.drain
  N12: S1.1, R1.Pin_0
  N13: S2.1, R2.Pin_0
